// Logisim project elaborato_VR421742_VR414014.circ as structural Verilog: 1 circuit, main circuit main
module main (
  input  in_1,
  input  in_2,
  input  in_3,
  output out_4,
  output out_5,
  output out_6,
  output out_7,
  output out_8,
  output out_9
);

  wire _001_out, and_1_out, EM_out, errore_out, j_k_ff_1_qn, not_1_out, not_2_out, not_5_out, not_8_out,
       ok_2_out, ok_3_out, ok_out, QI_out, QO_out, rotto_2_out, rotto_out, s_r_ff_1_qn, start_out,
       subtractor_1_bout, undriven;
  wire [0:0] comparator_1_lt;
  wire [7:0] comparator_1_gt, subtractor_1_out;

  J_K_Flip_Flop j_k_ff_1 (.K(in_1), .Qn(j_k_ff_1_qn));  // open: J, clk, Q, preset, en, reset
  not not_1 (not_1_out, _001_out);
  and _001 (_001_out, out_6, out_5, out_4);
  and start (start_out, in_1, in_1, in_1);
  // AND_Gate _010 is placed but not wired
  S_R_Flip_Flop s_r_ff_1 (.R(not_1_out), .Qn(s_r_ff_1_qn));  // open: S, clk, Q, preset, reset, en
  // AND_Gate _101 is placed but not wired
  // AND_Gate _110 is placed but not wired
  and and_1 (and_1_out, start_out, s_r_ff_1_qn);
  // OR_Gate iniziare is placed but not wired
  LED GA (.in(and_1_out));
  Counter NA (.load(and_1_out));  // open: D, count, Q, carry, clk, clr
  D_Flip_Flop d_ff_1 (.clk(in_1));  // open: D, Q, Qn, preset, en, reset
  Button QI (.out(QI_out));
  LED GB (.in(rotto_out));
  not not_2 (not_2_out, QI_out);
  and rotto (rotto_out, and_1_out, not_2_out);
  Hex_Digit_Display hex_digit_display_1 (.dp(undriven));  // open: value
  not not_3 (out_5, out_5);
  not not_4 (out_6, out_5);
  Comparator comparator_1 (.gt(comparator_1_gt[0]), .eq(out_5), .lt(comparator_1_lt[0]));  // open: a, b
  and ok (ok_out, QI_out, and_1_out);
  LED GC (.in(ok_out));
  Counter NC (.load(ok_out));  // open: D, count, Q, carry, clk, clr
  Subtractor subtractor_1 (.out(subtractor_1_out), .bin(undriven), .bout(subtractor_1_bout));  // open: a, b
  Counter #(.max('hc8), .ongoal("stay")) N_scrach (
    .load(subtractor_1_bout), .Q(comparator_1_gt));  // open: D, count, carry, clk, clr
  LED GD (.in(ok_2_out));
  Hex_Digit_Display hex_digit_display_2 (.value(subtractor_1_out[3:0]), .dp(ok_2_out));
  Button EM (.out(EM_out));
  not not_5 (not_5_out, EM_out);
  and ok_2 (ok_2_out, EM_out, ok_out);
  and errore (errore_out, not_5_out, ok_out);
  LED led_1 ();  // open: in
  J_K_Flip_Flop j_k_ff_2 (.J(errore_out), .Qn(out_4));  // open: clk, K, Q, preset, en, reset
  not not_6 (out_5, out_4);
  not not_7 (out_6, out_4);
  Button QO (.out(QO_out));
  not not_8 (not_8_out, QO_out);
  and ok_3 (ok_3_out, QO_out, ok_2_out);
  and rotto_2 (rotto_2_out, not_8_out, ok_2_out);
  or or_1 (j_k_ff_1_qn, rotto_2_out, ok_3_out);
  LED GF (.in(ok_3_out));
  LED GE (.in(rotto_2_out));
  Counter NF (.load(ok_3_out));  // open: D, count, Q, carry, clk, clr
  Counter NE (.load(rotto_2_out));  // open: D, count, Q, carry, clk, clr
  // Pins of 1 and 8 bits meet at comparator_1_gt
  // Pins of 4 and 8 bits meet at subtractor_1_out
  // Pins of 1 and 8 bits meet at {7'b1100100, comparator_1_lt[0]}

  assign in_2 = in_1;
  assign in_3 = in_1;
  assign out_7 = out_6;
  assign out_8 = out_5;
  assign out_9 = out_4;
  // also tied to GND on the sheet: comparator_1_lt[0]

  // Notes on the sheet:
  //   starter
  //   errors to stop
  //   errors types
  //   001: errore milling
  //   010: troppo scarto TOOerr
  //   110: everload di scarti NEerr
  //   101: overload di un counter NBerr
  //   cutting too much
  //   ispezione before
  //   VIN
  //   VOUT
  //   milling machine
  //   no gate
  //   control after
endmodule
